// Digital circuit Clock.dig as structural Verilog
module Clock (
  input  Debug,
  input  Run,
  input  Slow,
  input  Fast,
  input  Step,
  input  WCLK,
  input  SCLK,
  input  FCLK,
  output CLK,
  output CLK_2
);

  wire _7402_1_pin1, _7402_1_pin3, _7402_1_pin9, _7402_1_pin10;

  _7402 _7402_1 (
    .pin1(_7402_1_pin1), .pin2(Slow), .pin3(_7402_1_pin3), .pin4(_7402_1_pin3), .pin5(_7402_1_pin1),
    .pin6(Fast), .pin7(1'b0), .pin8(Run), .pin9(_7402_1_pin9), .pin10(_7402_1_pin10), .pin11(_7402_1_pin10),
    .pin12(Debug), .pin13(_7402_1_pin9), .pin14(1'b1));
  _74151 _74151_1 (
    .pin1(FCLK), .pin2(SCLK), .pin3(WCLK), .pin4(Step), .pin5(CLK), .pin6(CLK_2), .pin7(1'b0), .pin8(1'b0),
    .pin9(1'b0), .pin10(_7402_1_pin9), .pin11(_7402_1_pin1), .pin12(1'b0), .pin13(1'b0), .pin14(1'b0),
    .pin15(1'b0), .pin16(1'b1));

  // Notes on the sheet:
  //   WCLK: Watch clock, ~30 Hz
  //   SCLK: Slow Clock, ~ 1 KHz
  //   FCLK: Fast Clk, ~700 KHz
endmodule
